// Logisim project cpu.circ as structural Verilog
module half_adder (
  input  a,
  input  b,
  output sum,
  output carry
);

  xor xor_1 (sum, a, b);
  and and_1 (carry, b, a);
endmodule

module full_adder (
  input  a,
  input  b,
  input  carry_in,
  output sum,
  output carry_out
);

  wire half_adder_1_carry, half_adder_1_sum, half_adder_2_carry;

  half_adder half_adder_1 (.a(a), .b(b), .sum(half_adder_1_sum), .carry(half_adder_1_carry));
  half_adder half_adder_2 (.a(half_adder_1_sum), .b(carry_in), .sum(sum), .carry(half_adder_2_carry));
  or or_1 (carry_out, half_adder_2_carry, half_adder_1_carry);
endmodule

module byte_adder (
  input  carry_in,
  input  in_2,
  input  in_3,
  input  in_4,
  input  in_5,
  input  in_6,
  input  in_7,
  input  in_8,
  input  in_9,
  input  in_10,
  input  in_11,
  input  in_12,
  input  in_13,
  input  in_14,
  input  in_15,
  input  in_16,
  input  in_17,
  output out_18,
  output out_19,
  output out_20,
  output out_21,
  output out_22,
  output out_23,
  output out_24,
  output out_25,
  output out_26
);

  wire nibble_adder_1_carry_out;

  nibble_adder nibble_adder_1 (
    .carry(carry_in), .a_0(in_2), .a_1(in_3), .a_2(in_4), .a_3(in_5), .b_0(in_10), .b_1(in_11), .b_2(in_12),
    .b_3(in_13), .sum_0(out_18), .sum_1(out_19), .sum_2(out_20), .sum_3(out_21),
    .carry_out(nibble_adder_1_carry_out));
  nibble_adder nibble_adder_2 (
    .carry(nibble_adder_1_carry_out), .a_0(in_6), .a_1(in_7), .a_2(in_8), .a_3(in_9), .b_0(in_14),
    .b_1(in_15), .b_2(in_16), .b_3(in_17), .sum_0(out_22), .sum_1(out_23), .sum_2(out_24), .sum_3(out_25),
    .carry_out(out_26));
endmodule

module nibble_adder (
  input  carry,
  input  a_0,
  input  a_1,
  input  a_2,
  input  a_3,
  input  b_0,
  input  b_1,
  input  b_2,
  input  b_3,
  output sum_0,
  output sum_1,
  output sum_2,
  output sum_3,
  output carry_out
);

  wire full_adder_1_carry_out, full_adder_2_carry_out, full_adder_3_carry_out;

  full_adder full_adder_1 (.a(a_0), .b(b_0), .carry_in(carry), .sum(sum_0), .carry_out(full_adder_1_carry_out));
  full_adder full_adder_2 (
    .a(a_1), .b(b_1), .carry_in(full_adder_1_carry_out), .sum(sum_1), .carry_out(full_adder_2_carry_out));
  full_adder full_adder_3 (
    .a(a_2), .b(b_2), .carry_in(full_adder_2_carry_out), .sum(sum_2), .carry_out(full_adder_3_carry_out));
  full_adder full_adder_4 (.a(a_3), .b(b_3), .carry_in(full_adder_3_carry_out), .sum(sum_3), .carry_out(carry_out));
endmodule
